# Fritzing sketch 40106 1 Osc (saved by Fritzing 0.9.3b)
breadboards: 1

parts:
  IC1 = IC, DIP package, 14 pins [chip_label=IC]
  U2 = POT [package=alps_pot]
  AMPHENOL_-_ACJS-MHDR_-_JACK_6_35MM1 = AMPHENOL - ACJS-MHDR [package=ACJS-MHDR]
  C1 = Electrolytic Capacitor [capacitance=1µF package="100 mil [THT, electrolytic]"]
  BAT1 = BC9VPC [package=bc9vpc]

nets:
  N1: IC1.pin1, U2.A, C1.+
  N2: IC1.pin2, U2.S, AMPHENOL_-_ACJS-MHDR_-_JACK_6_35MM1.Tip_(3)
  N3: IC1.pin7, AMPHENOL_-_ACJS-MHDR_-_JACK_6_35MM1.Sleeve_(1), C1.-, BAT1.V-
  N4: IC1.pin14, BAT1.V+
